# Fritzing sketch ZX_Keyboard_1_1 (saved by Fritzing 0.9.0b)
breadboards: 1

parts:
  U2 = USB+SHIELD [package=usb-b-pth]
  R1 = Resistor [tolerance=±5% resistance=2.2k package=THT]
  R3 = Resistor [tolerance=±5% resistance=68 package=THT]
  D1 = Zener Diode [part_number=3V6 breakdown_voltage=3.6V package="Melf DO-213 AB [SMD]"]
  D2 = Zener Diode [part_number=3V6 breakdown_voltage=3.6V package="Melf DO-213 AB [SMD]"]
  Keyboard_rows = Header 8 [package=bm08b-srss-tb]
  Keyboard_columns = Header 5 [package=1x05-1mm-ra]
  R2 = Resistor [tolerance=±5% resistance=68 package=THT]
  Part1 = Arduino Pro Mini v13
  PC_Emul_/_Direct = Toggle Switch [package=THT]

nets:
  N1: U2.D+, R3.Pin_1, D2.cathode
  N2: U2.D-, R1.Pin_1, D1.cathode, R2.Pin_1
  GND: U2.GND, D1.anode, D2.anode, Part1.GND, PC_Emul_/_Direct.L2
  N3: U2.VBUS, Part1.VCC
  N4: R1.Pin_0, Part1.D5_PWM
  N5: R3.Pin_0, Part1.D2
  N6: Keyboard_rows.1, Part1.A3
  N7: Keyboard_rows.2, Part1.A2
  N8: Keyboard_rows.3, Part1.A1
  N9: Keyboard_rows.4, Part1.A0
  N10: Keyboard_rows.5, Part1.D10_PWM/SS
  N11: Keyboard_rows.6, Part1.D11_PWM/MOSI
  N12: Keyboard_rows.7, Part1.D12/MISO
  N13: Keyboard_rows.8, Part1.D13/SCK
  N14: Keyboard_columns.1, Part1.D3_PWM
  N15: Keyboard_columns.2, Part1.D6_PWM
  N16: Keyboard_columns.3, Part1.D7
  N17: Keyboard_columns.4, Part1.D8
  N18: Keyboard_columns.5, Part1.D9_PWM
  N19: R2.Pin_0, Part1.D4
  N20: Part1.A4, PC_Emul_/_Direct.COM

notes:
  D+
  D-
  GND
  VCC
